# Fritzing sketch 18th_appjam (saved by Fritzing 0.9.3b)
breadboards: 1

parts:
  PIR1 = PIR sensor
  U1 = ESP8266 WiFi Module [part_number=ESP8266]
  DHT1 = DHT22 Humidity and Temperature Sensor
  부품1 = Arduino Uno (Rev3)
  R1 = Resistor [tolerance=±5% resistance=220 package=THT]
  R2 = Resistor [tolerance=±5% resistance=220 package=THT]
  LPD8806_RGB_LED_Strip1 = LPD8806 RGB LED Strip
  부품2 = Bluetooth HM-10

nets:
  VDD: PIR1.VDD, U1.VCC, U1.CH_PD, DHT1.VDD, 부품1.3V3, R1.Pin_0
  GND: PIR1.GND, U1.GPIO_0, U1.GND, DHT1.GND, 부품1.GND, LPD8806_RGB_LED_Strip1.GND, 부품2.GND
  N1: U1.RXD, 부품1.D0/RX
  N2: U1.TXD, 부품1.D1/TX
  N3: DHT1.DATA, R1.Pin_1
  N4: 부품1.A0, R2.Pin_1
  N5: 부품1.D9_PWM, LPD8806_RGB_LED_Strip1.DI
  5V: 부품1.5V, LPD8806_RGB_LED_Strip1.+5V, 부품2.VCC

notes:
  MQ-2 Sensor Wires
  R G
  R W
  R G

custom parts:
  ESP8266 WiFi Module: Generic WiFi Module based on the ESP8266 with onboard PCB antenna and UART communications
  LPD8806 RGB LED Strip: Digitally addressable RGB LED strip
